# Fritzing sketch Skhema_podklyuchenia_vsego (saved by Fritzing 0.9.3b)
breadboards: 2

parts:
  Часть1 = Arduino Uno (Rev3)
  J1 = Screw terminal - 2 pins [package=THT]
  LCM1602_IIC1 = LCM1602 IIC [part_number="LCM1602 IIC" chip_label="LCM1602 IIC" package="DIP (Dual Inline) [THT]"]
  LCD1 = LCD screen
  J2 = Piezo Speaker
  Q1 = MOSFET-NCHANNEL [package=to220v]
  R4 = Resistor [tolerance=±5% resistance=220 package=THT]
  R5 = Resistor [tolerance=±5% resistance=220 package=THT]
  S1 = Pushbutton [package="[THT]"]
  R6 = Resistor [tolerance=±5% resistance=220 package=THT]
  SW1 = ENCODER_RGB_CA [package=encoder_led_3]
  U1 = MAX6675 [package=so08]

nets:
  N1: Часть1.A2, J2.pin2
  N2: Часть1.A4/SDA, LCM1602_IIC1.SDA
  N3: Часть1.A5/SCL, LCM1602_IIC1.SCL
  N4: Часть1.D9_PWM, R4.Pin_0, R5.Pin_0
  N5: Часть1.D11_PWM/MOSI, SW1.A
  N6: Часть1.D12/MISO, SW1.B
  N7: Часть1.D13/SCK, SW1.C
  N8: Часть1.D2, S1.Pin_1, S1.Pin_2, R6.Pin_0
  N9: Часть1.D5_PWM, U1.MISO
  N10: Часть1.D6_PWM, U1.CS
  N11: Часть1.D7, U1.SCK
  N12: J1.pin1, U1.T+
  N13: J1.pin2, U1.VSS
  VSS: LCM1602_IIC1.VSS, LCD1.VSS
  VDD: LCM1602_IIC1.VDD, LCD1.VDD
  N14: LCM1602_IIC1.V0, LCD1.V0
  N15: LCM1602_IIC1.RS, LCD1.RS
  N16: LCM1602_IIC1.RW, LCD1.R/W
  N17: LCM1602_IIC1.E, LCD1.E
  N18: LCM1602_IIC1.D0, LCD1.DB0
  N19: LCM1602_IIC1.D1, LCD1.DB1
  N20: LCM1602_IIC1.D2, LCD1.DB2
  N21: LCM1602_IIC1.D3, LCD1.DB3
  N22: LCM1602_IIC1.D4, LCD1.DB4
  N23: LCM1602_IIC1.D5, LCD1.DB5
  N24: LCM1602_IIC1.D6, LCD1.DB6
  N25: LCM1602_IIC1.D7, LCD1.DB7
  N26: LCM1602_IIC1.A, LCD1.LED+
  N27: LCM1602_IIC1.K, LCD1.LED-
  N28: LCM1602_IIC1.GND, J2.pin1, R6.Pin_1, SW1.-B
  VCC: LCM1602_IIC1.VCC, S1.Pin_3, S1.Pin_4, SW1.+, U1.VDD
  N29: Q1.G, R4.Pin_1
  N30: Q1.S, R5.Pin_1

notes:
  Buzzer (пищалка)
  Нагрузка (спираль нагрева)
  100R
  10k
  N - MOSFET
  Кнопка СТАРТ/СТОП
  Энкодер
  10K
  Модуль MAX6675
  (было лень все дорисовывать, ибо готового варианта в этой проге нет, но, думаю, и так понятно; главное, что сигнальные идут на пины 5,6,7)
  Сюда термопару

custom parts:
  LCM1602 IIC: I2C-Module to use a 1602 or 2004 LCD on with the wire.h libory Serial LCD Modul
